// Logisim project Flyer1_HardwareCertified.circ as structural Verilog: 6 circuits, main circuit main
module main (
);

  wire and_1_out, and_2_out, and_3_out, and_4_out, and_5_out, and_6_out, and_7_out, and_8_out, and_9_out,
       and_10_out, and_11_out, and_12_out, and_13_out, and_14_out, and_15_out, and_16_out, and_17_out,
       and_18_out, and_19_out, and_20_out, and_21_out, and_22_out, and_23_out, and_24_out, and_25_out,
       and_26_out, and_27_out, and_28_out, and_29_out, and_30_out, and_31_out, and_32_out, and_33_out,
       and_34_out, and_35_out, and_36_out, and_37_out, and_38_out, AXC, AXI, AXO, AXS, clock_1_out,
       cu_1_counterreset, cu_1_halt, decoder_1_out0, decoder_1_out1, decoder_1_out2, decoder_1_out3,
       decoder_1_out4, decoder_1_out5, decoder_1_out6, decoder_1_out7, decoder_2_out0, decoder_2_out1,
       decoder_2_out2, decoder_2_out3, FC, FS, IAE, IAS, IRS, MAE, MDE, MDO, not_1_out, not_2_out, not_3_out,
       not_4_out, not_5_out, not_6_out, not_7_out, not_8_out, not_9_out, not_10_out, not_11_out, not_12_out,
       not_13_out, not_14_out, PAO, PAS, PCE, PCL, PCO, PDO, PDS, RR, RW, SPE, SPI, SPO, TXO, TXS;
  wire [1:0] ASEL;
  wire [2:0] Steps;
  wire [2:2] DSEL;
  wire [3:0] bit_extender_1_out;
  wire [6:0] alu_1_f, F;
  wire [7:0] DataSP, pull_resistor_15_node;
  wire [23:0] alu_1_s, controlled_buffer_2_out, controlled_buffer_4_out, controlled_buffer_8_out,
       controlled_buffer_10_out, controlled_buffer_12_out, controlled_buffer_13_out,
       controlled_buffer_14_out, controlled_buffer_15_out, controlled_buffer_19_out,
       controlled_buffer_21_out, controlled_buffer_25_out, controlled_buffer_27_out,
       controlled_buffer_29_out, controlled_buffer_30_out, controlled_buffer_33_out, DataAX, DataPC, DataTX,
       IA_q, Instr, ledbar_1_p3, Memory_dout, Peripherals, pull_resistor_25_node;

  Register #(.trigger("high"), .width(24)) TX (.D(Peripherals), .en(TXS), .clk(TXS), .Q(DataTX));  // open: clr
  assign Peripherals = TXO ? DataTX : 24'bz;  // Controlled_Buffer controlled_buffer_1
  Pull_Resistor pull_resistor_1 (.node(TXO));
  assign controlled_buffer_2_out = AXI ? Peripherals : 24'bz;  // Controlled_Buffer controlled_buffer_2
  Pull_Resistor pull_resistor_2 (.node(PDO));
  Pull_Resistor pull_resistor_3 (.node(PDS));
  ALU alu_1 (.A(Peripherals), .B(DataTX), .ALUE(Instr[23]), .INST(Instr[22:19]), .S(alu_1_s), .F(alu_1_f));
  Register #(.trigger("high"), .width(7)) FLAG (.D(alu_1_f), .en(FS), .clk(FS), .Q(F), .clr(FC));
  Register #(.trigger("high"), .width(24)) AX (.D(controlled_buffer_2_out), .en(AXS), .clk(AXS), .Q(DataAX), .clr(AXC));
  not not_1 (not_1_out, AXI);
  assign controlled_buffer_2_out = not_1_out ? alu_1_s : 24'bz;  // Controlled_Buffer controlled_buffer_3
  Decoder #(.enable("false"), .select(3)) decoder_1 (
    .out0(decoder_1_out0), .out1(decoder_1_out1), .out2(decoder_1_out2), .out3(decoder_1_out3),
    .out4(decoder_1_out4), .out5(decoder_1_out5), .out6(decoder_1_out6), .out7(decoder_1_out7),
    .sel({DSEL[2], ASEL}));
  and and_1 (and_1_out, PDS, decoder_1_out0);
  and and_2 (and_2_out, and_1_out, PDO);
  assign controlled_buffer_4_out = and_2_out ? Peripherals : 24'bz;  // Controlled_Buffer controlled_buffer_4
  Pull_Resistor pull_resistor_4 (.node(AXO));
  assign Peripherals = AXO ? DataAX : 24'bz;  // Controlled_Buffer controlled_buffer_5
  Pull_Resistor pull_resistor_5 (.node(Peripherals));
  Pull_Resistor pull_resistor_6 (.node(Peripherals));
  not not_2 (not_2_out, PDO);
  assign Peripherals = and_3_out ? controlled_buffer_4_out : 24'bz;  // Controlled_Buffer controlled_buffer_6
  and and_3 (and_3_out, not_2_out, and_1_out);
  Pull_Resistor pull_resistor_7 (.node(controlled_buffer_4_out));
  Register #(.trigger("high"), .width(24)) IR (
    .D(Peripherals), .en(IRS), .clk(IRS), .Q({Instr[23:19], DSEL[2], ASEL, Instr[15:0]}));  // open: clr
  and and_4 (and_4_out, PDS, decoder_1_out1);
  Pull_Resistor pull_resistor_8 (.node({Instr[23:19], DSEL[2], ASEL, Instr[15:0]}));
  Pull_Resistor pull_resistor_9 (.node(Peripherals));
  not not_3 (not_3_out, PDO);
  assign Peripherals = and_6_out ? controlled_buffer_8_out : 24'bz;  // Controlled_Buffer controlled_buffer_7
  and and_5 (and_5_out, and_4_out, PDO);
  and and_6 (and_6_out, not_3_out, and_4_out);
  assign controlled_buffer_8_out = and_5_out ? Peripherals : 24'bz;  // Controlled_Buffer controlled_buffer_8
  Pull_Resistor pull_resistor_10 (.node(controlled_buffer_8_out));
  Clock #(.highDuration(8), .lowDuration(8)) clock_1 (.out(clock_1_out));
  CU cu_1 (
    .Instruction({Instr[23:19], DSEL[2], ASEL, Instr[15]}), .Flags(F), .ClockCycle(Steps), .IRS(IRS),
    .PCL(PCL), .PCE(PCE), .SPO(SPO), .SPI(SPI), .SPE(SPE), .TXS(TXS), .TXO(TXO), .AXS(AXS), .AXI(AXI),
    .AXO(AXO), .AXC(AXC), .IAS(IAS), .IAE(IAE), .FS(FS), .FC(FC), .PDS(PDS), .PDO(PDO), .PAS(PAS), .PAO(PAO),
    .Halt(cu_1_halt), .CounterReset(cu_1_counterreset), .MAE(MAE), .MDE(MDE), .MDO(MDO), .RR(RR), .RW(RW),
    .PCO(PCO));
  and and_7 (and_7_out, PDS, decoder_1_out2);
  TIMU timu_1 (.Clock(clock_1_out), .Halt(cu_1_halt), .Reset(cu_1_counterreset), .StepOutput(Steps));
  Pull_Resistor pull_resistor_11 (.node(Peripherals));
  not not_4 (not_4_out, PDO);
  assign Peripherals = and_9_out ? controlled_buffer_10_out : 24'bz;  // Controlled_Buffer controlled_buffer_9
  and and_8 (and_8_out, and_7_out, PDO);
  and and_9 (and_9_out, not_4_out, and_7_out);
  assign controlled_buffer_10_out = and_8_out ? Peripherals : 24'bz;  // Controlled_Buffer controlled_buffer_10
  Pull_Resistor pull_resistor_12 (.node(controlled_buffer_10_out));
  and and_10 (and_10_out, PDS, decoder_1_out3);
  Register #(.trigger("high"), .width(24)) IA (.D(Peripherals), .en(IAS), .clk(IAS), .Q(IA_q));  // open: clr
  Pull_Resistor pull_resistor_13 (.node(Peripherals));
  not not_5 (not_5_out, PDO);
  assign Peripherals = and_12_out ? controlled_buffer_12_out : 24'bz;  // Controlled_Buffer controlled_buffer_11
  and and_11 (and_11_out, and_10_out, PDO);
  assign controlled_buffer_12_out = and_11_out ? Peripherals : 24'bz;  // Controlled_Buffer controlled_buffer_12
  Pull_Resistor pull_resistor_14 (.node(controlled_buffer_12_out));
  Counter #(.max('hffffff), .width(24)) PC (
    .load(PCL), .up(1'b1), .count(PCE), .clk(clock_1_out), .D(controlled_buffer_13_out), .Q(DataPC));  // open: clr, carry
  assign controlled_buffer_13_out = PCL ? controlled_buffer_14_out : 24'bz;  // Controlled_Buffer controlled_buffer_13
  Counter SP (
    .load(1'b0), .up(SPI), .count(SPE), .clk(clock_1_out), .D(pull_resistor_15_node), .Q(DataSP));  // open: clr, carry
  Pull_Resistor pull_resistor_15 (.node(pull_resistor_15_node));
  assign controlled_buffer_14_out = IAE ? IA_q : 24'bz;  // Controlled_Buffer controlled_buffer_14
  Pull_Resistor pull_resistor_16 (.node(IAE));
  and and_12 (and_12_out, not_5_out, and_10_out);
  and and_13 (and_13_out, PDS, decoder_1_out4);
  and and_14 (and_14_out, and_13_out, PDO);
  assign controlled_buffer_15_out = and_14_out ? Peripherals : 24'bz;  // Controlled_Buffer controlled_buffer_15
  Pull_Resistor pull_resistor_17 (.node(Peripherals));
  not not_6 (not_6_out, PDO);
  assign Peripherals = and_15_out ? controlled_buffer_15_out : 24'bz;  // Controlled_Buffer controlled_buffer_16
  and and_15 (and_15_out, not_6_out, and_13_out);
  Pull_Resistor pull_resistor_18 (.node(controlled_buffer_15_out));
  Pull_Resistor pull_resistor_19 (.node(PCO));
  assign controlled_buffer_14_out = PCO ? DataPC : 24'bz;  // Controlled_Buffer controlled_buffer_17
  Pull_Resistor pull_resistor_20 (.node(SPO));
  assign controlled_buffer_14_out = SPO ? {{16{1'b1}}, DataSP} : 24'bz;  // Controlled_Buffer controlled_buffer_18
  Pull_Resistor pull_resistor_21 (.node(controlled_buffer_14_out));
  and and_16 (and_16_out, PDS, decoder_1_out5);
  Pull_Resistor pull_resistor_22 (.node(MDE));
  Pull_Resistor pull_resistor_23 (.node(MDO));
  Pull_Resistor pull_resistor_24 (.node(MAE));
  assign controlled_buffer_19_out = MAE ? controlled_buffer_14_out : 24'bz;  // Controlled_Buffer controlled_buffer_19
  Pull_Resistor pull_resistor_25 (.node(pull_resistor_25_node));
  Pull_Resistor pull_resistor_26 (.node(Peripherals));
  not not_7 (not_7_out, PDO);
  assign Peripherals = and_18_out ? controlled_buffer_21_out : 24'bz;  // Controlled_Buffer controlled_buffer_20
  and and_17 (and_17_out, and_16_out, PDO);
  and and_18 (and_18_out, not_7_out, and_16_out);
  assign controlled_buffer_21_out = and_17_out ? Peripherals : 24'bz;  // Controlled_Buffer controlled_buffer_21
  Pull_Resistor pull_resistor_27 (.node(controlled_buffer_21_out));
  not not_8 (not_8_out, MDO);
  and and_19 (and_19_out, MDE, not_8_out);
  assign pull_resistor_25_node = and_19_out ? Peripherals : 24'bz;  // Controlled_Buffer controlled_buffer_22
  RAM #(.addrWidth(24), .dataWidth(24), .trigger("high"), .\type ("nonvolatile")) Memory (
    .addr(controlled_buffer_19_out), .we(RW), .oe(RR), .din(pull_resistor_25_node), .dout(Memory_dout));
  Pull_Resistor pull_resistor_28 (.node(controlled_buffer_19_out));
  Pull_Resistor pull_resistor_29 (.node(RW));
  Pull_Resistor pull_resistor_30 (.node(RR));
  and and_20 (and_20_out, PDS, decoder_1_out6);
  assign Peripherals = and_21_out ? Memory_dout : 24'bz;  // Controlled_Buffer controlled_buffer_23
  and and_21 (and_21_out, MDE, MDO);
  Pull_Resistor pull_resistor_31 (.node(Peripherals));
  not not_9 (not_9_out, PDO);
  assign Peripherals = and_23_out ? controlled_buffer_25_out : 24'bz;  // Controlled_Buffer controlled_buffer_24
  and and_22 (and_22_out, and_20_out, PDO);
  and and_23 (and_23_out, not_9_out, and_20_out);
  assign controlled_buffer_25_out = and_22_out ? Peripherals : 24'bz;  // Controlled_Buffer controlled_buffer_25
  Pull_Resistor pull_resistor_32 (.node(controlled_buffer_25_out));
  and and_24 (and_24_out, PDS, decoder_1_out7);
  Pull_Resistor pull_resistor_33 (.node(Peripherals));
  not not_10 (not_10_out, PDO);
  assign Peripherals = and_27_out ? controlled_buffer_27_out : 24'bz;  // Controlled_Buffer controlled_buffer_26
  and and_25 (and_25_out, and_24_out, PDO);
  assign controlled_buffer_27_out = and_25_out ? Peripherals : 24'bz;  // Controlled_Buffer controlled_buffer_27
  Pull_Resistor pull_resistor_34 (.node(controlled_buffer_27_out));
  Decoder #(.enable("false"), .select(2)) decoder_2 (
    .out0(decoder_2_out0), .out1(decoder_2_out1), .out2(decoder_2_out2), .out3(decoder_2_out3), .sel(ASEL));
  Pull_Resistor pull_resistor_35 (.node(PAO));
  Pull_Resistor pull_resistor_36 (.node(PAS));
  and and_26 (and_26_out, PAS, decoder_2_out0);
  and and_27 (and_27_out, not_10_out, and_24_out);
  Pull_Resistor pull_resistor_37 (.node(Peripherals));
  not not_11 (not_11_out, PAO);
  assign Peripherals = and_29_out ? controlled_buffer_29_out : 24'bz;  // Controlled_Buffer controlled_buffer_28
  and and_28 (and_28_out, and_26_out, PAO);
  and and_29 (and_29_out, not_11_out, and_26_out);
  assign controlled_buffer_29_out = and_28_out ? Peripherals : 24'bz;  // Controlled_Buffer controlled_buffer_29
  Pull_Resistor pull_resistor_38 (.node(controlled_buffer_29_out));
  Hex_Digit_Display #(.decimalPoint("false")) hex_digit_display_1 (.value(Instr[23:20]));
  Hex_Digit_Display #(.decimalPoint("false")) hex_digit_display_2 (.value({Instr[19], DSEL[2], ASEL}));
  Hex_Digit_Display #(.decimalPoint("false")) hex_digit_display_3 (.value(DataAX[23:20]));
  Hex_Digit_Display #(.decimalPoint("false")) hex_digit_display_4 (.value(DataAX[19:16]));
  Hex_Digit_Display #(.decimalPoint("false")) hex_digit_display_5 (.value(DataPC[23:20]));
  Hex_Digit_Display #(.decimalPoint("false")) hex_digit_display_6 (.value(DataPC[19:16]));
  Hex_Digit_Display #(.decimalPoint("false")) hex_digit_display_7 (.value(Instr[15:12]));
  Hex_Digit_Display #(.decimalPoint("false")) hex_digit_display_8 (.value(Instr[11:8]));
  Hex_Digit_Display #(.decimalPoint("false")) hex_digit_display_9 (.value(DataAX[15:12]));
  Hex_Digit_Display #(.decimalPoint("false")) hex_digit_display_10 (.value(DataAX[11:8]));
  Hex_Digit_Display #(.decimalPoint("false")) hex_digit_display_11 (.value(DataPC[15:12]));
  Hex_Digit_Display #(.decimalPoint("false")) hex_digit_display_12 (.value(DataPC[11:8]));
  Pull_Resistor pull_resistor_39 (.node(Peripherals));
  and and_30 (and_30_out, PAS, decoder_2_out1);
  not not_12 (not_12_out, PAO);
  and and_31 (and_31_out, and_30_out, PAO);
  assign controlled_buffer_30_out = and_31_out ? Peripherals : 24'bz;  // Controlled_Buffer controlled_buffer_30
  Pull_Resistor pull_resistor_40 (.node(controlled_buffer_30_out));
  Hex_Digit_Display #(.decimalPoint("false")) hex_digit_display_13 (.value(Instr[7:4]));
  Hex_Digit_Display #(.decimalPoint("false")) hex_digit_display_14 (.value(Instr[3:0]));
  Hex_Digit_Display #(.decimalPoint("false")) hex_digit_display_15 (.value(DataAX[7:4]));
  Hex_Digit_Display #(.decimalPoint("false")) hex_digit_display_16 (.value(DataAX[3:0]));
  Hex_Digit_Display #(.decimalPoint("false")) hex_digit_display_17 (.value(DataPC[7:4]));
  Hex_Digit_Display #(.decimalPoint("false")) hex_digit_display_18 (.value(DataPC[3:0]));
  assign Peripherals = and_32_out ? controlled_buffer_30_out : 24'bz;  // Controlled_Buffer controlled_buffer_31
  and and_32 (and_32_out, not_12_out, and_30_out);
  and and_33 (and_33_out, PAS, decoder_2_out2);
  and and_34 (and_34_out, and_33_out, PAO);
  assign bit_extender_1_out = {{1{1'b0}}, Steps};  // Bit_Extender bit_extender_1
  Hex_Digit_Display #(.decimalPoint("false")) hex_digit_display_19 (.value(DataTX[23:20]));
  Hex_Digit_Display #(.decimalPoint("false")) hex_digit_display_20 (.value(4'b1111));
  Pull_Resistor pull_resistor_41 (.node(Peripherals));
  not not_13 (not_13_out, PAO);
  assign Peripherals = and_35_out ? controlled_buffer_33_out : 24'bz;  // Controlled_Buffer controlled_buffer_32
  and and_35 (and_35_out, not_13_out, and_33_out);
  assign controlled_buffer_33_out = and_34_out ? Peripherals : 24'bz;  // Controlled_Buffer controlled_buffer_33
  Pull_Resistor pull_resistor_42 (.node(controlled_buffer_33_out));
  Hex_Digit_Display #(.decimalPoint("false")) hex_digit_display_21 (.value(bit_extender_1_out));
  Hex_Digit_Display #(.decimalPoint("false")) hex_digit_display_22 (.value(DataTX[19:16]));
  Hex_Digit_Display #(.decimalPoint("false")) hex_digit_display_23 (.value(DataTX[15:12]));
  Hex_Digit_Display #(.decimalPoint("false")) hex_digit_display_24 (.value(4'b1111));
  Hex_Digit_Display #(.decimalPoint("false")) hex_digit_display_25 (.value(4'b1111));
  and and_36 (and_36_out, PAS, decoder_2_out3);
  // LedBar #(.inputtype("row"), .matrixcols(7)) ledbar_1: pin names not known; wires that end beside it: controlled_buffer_33_out, F, ledbar_1_p3
  Hex_Digit_Display #(.decimalPoint("false")) hex_digit_display_26 (.value(DataTX[11:8]));
  Hex_Digit_Display #(.decimalPoint("false")) hex_digit_display_27 (.value(DataTX[7:4]));
  Hex_Digit_Display #(.decimalPoint("false")) hex_digit_display_28 (.value(4'b1111));
  Hex_Digit_Display #(.decimalPoint("false")) hex_digit_display_29 (.value(DataSP[7:4]));
  Pull_Resistor pull_resistor_43 (.node(Peripherals));
  not not_14 (not_14_out, PAO);
  assign Peripherals = and_38_out ? ledbar_1_p3 : 24'bz;  // Controlled_Buffer controlled_buffer_34
  and and_37 (and_37_out, and_36_out, PAO);
  and and_38 (and_38_out, not_14_out, and_36_out);
  assign ledbar_1_p3 = and_37_out ? Peripherals : 24'bz;  // Controlled_Buffer controlled_buffer_35
  Pull_Resistor pull_resistor_44 (.node(ledbar_1_p3));
  Hex_Digit_Display #(.decimalPoint("false")) hex_digit_display_30 (.value(DataTX[3:0]));
  Hex_Digit_Display #(.decimalPoint("false")) hex_digit_display_31 (.value(DataSP[3:0]));

  // Other names for the same wires on the sheet: DSEL[1:0] = ASEL; Instr[18:16] = {DSEL[2], ASEL}

  // Notes on the sheet:
  //   19/04/2024: HARDWARE TEST MASIH MENEMUKAN ISSUE DI SMEUA INSTRUKSI MATH (80XXXX - FFXXXXX). 
  //   INSTRUCTION REGISTER
  //   ACCUMULATOR
  //   PROGRAM COUNTER
  //   CLOCKSTEP
  //   TEMPORARY
  //   STACK POINTER
  //   FLAGS
endmodule

module ALU (
  input  ALUE,
  input  [3:0] INST,
  input  [23:0] A,
  input  [23:0] B,
  output [23:0] S,
  output [6:0] F
);

  wire decoder_1_out0, decoder_1_out1, decoder_1_out2, decoder_1_out3, decoder_1_out4, decoder_1_out5,
       decoder_1_out6, decoder_1_out7, decoder_1_out10, decoder_1_out11, decoder_1_out12, decoder_1_out13,
       or_1_out, or_2_out;
  wire [23:0] adder_1_out, and_1_out, bit_extender_1_out, divider_1_out, multiplier_1_out, not_1_out,
       or_3_out, shifter_1_out, shifter_2_out, shifter_3_out, shifter_4_out, xor_1_out, xor_2_out;

  Decoder #(.select(4)) decoder_1 (
    .out0(decoder_1_out0), .out1(decoder_1_out1), .out2(decoder_1_out2), .out3(decoder_1_out3),
    .out4(decoder_1_out4), .out5(decoder_1_out5), .out6(decoder_1_out6), .out7(decoder_1_out7),
    .out10(decoder_1_out10), .out11(decoder_1_out11), .out12(decoder_1_out12), .out13(decoder_1_out13),
    .sel(INST), .en(ALUE));  // open: out8, out9, out14, out15
  assign bit_extender_1_out = {{23{decoder_1_out1}}, decoder_1_out1};  // Bit_Extender bit_extender_1
  Multiplier #(.mode("twosComplement"), .width(24)) multiplier_1 (
    .a(A), .b(B), .out(multiplier_1_out));  // open: cin, cout
  assign and_1_out = A & B;  // AND_Gate and_1, 24 bits wide
  assign xor_1_out = A ^ B;  // XOR_Gate xor_1, 24 bits wide
  Shifter #(.width(24)) shifter_1 (.in(A), .\dist (B[4:0]), .out(shifter_1_out));
  assign S = decoder_1_out11 ? shifter_2_out : 24'bz;  // Controlled_Buffer controlled_buffer_1
  Shifter #(.shift("lr"), .width(24)) shifter_2 (.\dist (B[4:0]), .out(shifter_2_out));  // open: in
  assign xor_2_out = B ^ bit_extender_1_out;  // XOR_Gate xor_2, 24 bits wide
  assign S = decoder_1_out2 ? multiplier_1_out : 24'bz;  // Controlled_Buffer controlled_buffer_2
  assign S = decoder_1_out4 ? and_1_out : 24'bz;  // Controlled_Buffer controlled_buffer_3
  assign S = decoder_1_out6 ? xor_1_out : 24'bz;  // Controlled_Buffer controlled_buffer_4
  or or_1 (or_1_out, A[12], A[23], A[22], A[21], A[20], A[19], A[18], A[17], A[16], A[15], A[14], A[13], A[11], A[10], A[9], A[8], A[7], A[6], A[5], A[4], A[3], A[2], A[1], A[0]);
  assign S = decoder_1_out10 ? shifter_1_out : 24'bz;  // Controlled_Buffer controlled_buffer_5
  or or_2 (or_2_out, decoder_1_out0, decoder_1_out1);
  assign S = or_2_out ? adder_1_out : 24'bz;  // Controlled_Buffer controlled_buffer_6
  Adder #(.width(24)) adder_1 (.a(A), .b(xor_2_out), .out(adder_1_out), .cin(decoder_1_out1), .cout(F[6]));
  assign S = decoder_1_out3 ? divider_1_out : 24'bz;  // Controlled_Buffer controlled_buffer_7
  Divider #(.mode("twosComplement"), .width(24)) divider_1 (.a(A), .b(B), .out(divider_1_out));  // open: upper, rem
  assign or_3_out = A | B;  // OR_Gate or_3, 24 bits wide
  assign S = decoder_1_out5 ? or_3_out : 24'bz;  // Controlled_Buffer controlled_buffer_8
  assign not_1_out = ~A;  // NOT_Gate not_1, 24 bits wide
  assign S = decoder_1_out7 ? not_1_out : 24'bz;  // Controlled_Buffer controlled_buffer_9
  Comparator #(.width(24)) comparator_1 (.a(A), .b(B), .gt(F[5]), .eq(F[4]));  // open: lt
  not not_2 (F[3], or_1_out);
  assign S = decoder_1_out12 ? shifter_3_out : 24'bz;  // Controlled_Buffer controlled_buffer_10
  Shifter #(.shift("rl"), .width(24)) shifter_3 (.in(A), .\dist (B[4:0]), .out(shifter_3_out));
  assign S = decoder_1_out13 ? shifter_4_out : 24'bz;  // Controlled_Buffer controlled_buffer_11
  Shifter #(.shift("rr"), .width(24)) shifter_4 (.\dist (B[4:0]), .out(shifter_4_out));  // open: in
  Pull_Resistor pull_resistor_1 (.node(S));
  Pull_Resistor pull_resistor_2 (.node(F[0]));

  assign F[2:1] = {A[23], A[0]};
endmodule

module CU (
  input  [8:0] Instruction,
  input  [2:0] ClockCycle,
  input  [6:0] Flags,
  output IRS,
  output MAE,
  output MDE,
  output MDO,
  output RR,
  output RW,
  output PCO,
  output PCL,
  output PCE,
  output SPO,
  output SPI,
  output SPE,
  output TXS,
  output TXO,
  output AXS,
  output AXI,
  output AXO,
  output AXC,
  output IAS,
  output IAE,
  output FS,
  output FC,
  output PDS,
  output PDO,
  output PAS,
  output PAO,
  output Halt,
  output CounterReset
);

  wire and_1_out, and_2_out, and_3_out, and_4_out, and_5_out, and_6_out, and_7_out, and_8_out, and_9_out,
       and_10_out, and_11_out, and_12_out, and_13_out, and_14_out, and_15_out, and_16_out, and_17_out,
       and_18_out, and_19_out, and_20_out, and_21_out, and_22_out, and_23_out, and_24_out, and_25_out,
       and_26_out, and_27_out, and_28_out, and_29_out, and_30_out, and_31_out, and_32_out, and_33_out,
       and_35_out, and_36_out, and_37_out, and_39_out, and_40_out, and_41_out, and_43_out, and_45_out,
       and_46_out, and_47_out, and_48_out, and_49_out, and_51_out, and_52_out, and_53_out, and_54_out,
       and_55_out, and_56_out, and_57_out, and_58_out, and_59_out, and_60_out, and_61_out, and_62_out,
       and_63_out, and_64_out, and_65_out, and_66_out, and_67_out, and_68_out, and_69_out, and_70_out,
       and_71_out, and_72_out, and_73_out, and_74_out, and_76_out, and_77_out, and_78_out, and_79_out,
       and_80_out, and_81_out, and_82_out, and_83_out, buffer_1_out, buffer_2_out, buffer_3_out,
       buffer_4_out, buffer_5_out, buffer_6_out, buffer_7_out, buffer_8_out, buffer_9_out, buffer_10_out,
       buffer_11_out, buffer_12_out, buffer_13_out, buffer_14_out, buffer_15_out, buffer_16_out,
       buffer_17_out, buffer_18_out, buffer_19_out, buffer_20_out, buffer_21_out, buffer_22_out,
       buffer_23_out, buffer_24_out, buffer_25_out, buffer_26_out, buffer_27_out, buffer_28_out,
       buffer_29_out, buffer_30_out, buffer_31_out, buffer_32_out, buffer_33_out, buffer_34_out,
       buffer_35_out, buffer_36_out, buffer_37_out, buffer_38_out, buffer_39_out, buffer_40_out,
       buffer_41_out, buffer_42_out, buffer_43_out, buffer_44_out, buffer_45_out, buffer_46_out,
       buffer_47_out, buffer_48_out, not_1_out, or_1_out, or_2_out, or_3_out, or_4_out;
  wire [6:0] decoder_1_out7;
  wire [15:0] decoder_2_out15, decoder_3_out15;

  and and_1 (and_1_out, ~Instruction[3], ~Instruction[2], Flags[6], ~Instruction[1], ~Instruction[0]);  // AND_Gate
  and and_2 (and_2_out, ~Instruction[3], ~Instruction[2], ~Flags[6], ~Instruction[1], Instruction[0]);  // AND_Gate
  and and_3 (and_3_out, ~Instruction[3], ~Instruction[2], Flags[5], Instruction[1], ~Instruction[0]);  // AND_Gate
  and and_4 (and_4_out, ~Instruction[3], ~Instruction[2], ~Flags[5], Instruction[1], Instruction[0]);  // AND_Gate
  and and_5 (and_5_out, ~Instruction[3], Instruction[2], Flags[4], ~Instruction[1], ~Instruction[0]);  // AND_Gate
  and and_6 (and_6_out, ~Instruction[3], Instruction[2], ~Flags[4], ~Instruction[1], Instruction[0]);  // AND_Gate
  and and_7 (and_7_out, ~Instruction[3], Instruction[2], Flags[3], Instruction[1], ~Instruction[0]);  // AND_Gate
  and and_8 (and_8_out, ~Instruction[3], Instruction[2], ~Flags[3], Instruction[1], Instruction[0]);  // AND_Gate
  and and_9 (and_9_out, Instruction[3], ~Instruction[2], Flags[2], ~Instruction[1], ~Instruction[0]);  // AND_Gate
  and and_10 (and_10_out, Instruction[3], ~Instruction[2], ~Flags[2], ~Instruction[1], Instruction[0]);  // AND_Gate
  and and_11 (and_11_out, Instruction[3], ~Instruction[2], Flags[1], Instruction[1], ~Instruction[0]);  // AND_Gate
  and and_12 (and_12_out, Instruction[3], ~Instruction[2], ~Flags[1], Instruction[1], Instruction[0]);  // AND_Gate
  and and_13 (and_13_out, Instruction[3], Instruction[2], Flags[0], ~Instruction[1], ~Instruction[0]);  // AND_Gate
  and and_14 (and_14_out, Instruction[3], Instruction[2], ~Flags[0], ~Instruction[1], Instruction[0]);  // AND_Gate
  or or_1 (or_1_out, and_1_out, and_2_out, and_3_out, and_4_out, and_5_out, and_6_out, and_7_out, and_8_out, and_9_out, and_10_out, and_11_out, and_12_out, and_13_out, and_14_out);
  Decoder #(.enable("false"), .select(3)) decoder_1 (
    .out0(IRS), .out1(decoder_1_out7[6]), .out2(decoder_1_out7[5]), .out3(decoder_1_out7[4]),
    .out4(decoder_1_out7[3]), .out5(decoder_1_out7[2]), .out6(decoder_1_out7[1]), .out7(decoder_1_out7[0]),
    .sel(ClockCycle));
  Pull_Resistor pull_resistor_1 (.node(or_1_out));
  not not_1 (not_1_out, Instruction[8]);
  Decoder #(.select(4)) decoder_2 (
    .out0(decoder_2_out15[15]), .out1(decoder_2_out15[14]), .out2(decoder_2_out15[13]),
    .out3(decoder_2_out15[12]), .out4(decoder_2_out15[11]), .out5(decoder_2_out15[10]),
    .out6(decoder_2_out15[9]), .out7(decoder_2_out15[8]), .out8(decoder_2_out15[7]),
    .out9(decoder_2_out15[6]), .out10(decoder_2_out15[5]), .out11(decoder_2_out15[4]),
    .out12(decoder_2_out15[3]), .out13(decoder_2_out15[2]), .out14(decoder_2_out15[1]),
    .out15(decoder_2_out15[0]), .sel(Instruction[7:4]), .en(not_1_out));
  Decoder #(.select(4)) decoder_3 (
    .out0(decoder_3_out15[15]), .out1(decoder_3_out15[14]), .out2(decoder_3_out15[13]),
    .out3(decoder_3_out15[12]), .out4(decoder_3_out15[11]), .out5(decoder_3_out15[10]),
    .out6(decoder_3_out15[9]), .out7(decoder_3_out15[8]), .out8(decoder_3_out15[7]),
    .out9(decoder_3_out15[6]), .out10(decoder_3_out15[5]), .out11(decoder_3_out15[4]),
    .out12(decoder_3_out15[3]), .out13(decoder_3_out15[2]), .out14(decoder_3_out15[1]),
    .out15(decoder_3_out15[0]), .sel(Instruction[7:4]), .en(Instruction[8]));
  or or_2 (or_2_out, decoder_3_out15[15], decoder_3_out15[14], decoder_3_out15[13], decoder_3_out15[12], decoder_3_out15[7], decoder_3_out15[6], decoder_3_out15[5], decoder_3_out15[4]);
  or or_3 (or_3_out, decoder_3_out15[11], decoder_3_out15[10], decoder_3_out15[9], decoder_3_out15[8], decoder_3_out15[2], decoder_3_out15[1], decoder_3_out15[0]);
  and and_15 (and_15_out, decoder_2_out15[15], decoder_1_out7[6]);
  and and_16 (and_16_out, decoder_2_out15[15], decoder_1_out7[5]);
  and and_17 (and_17_out, decoder_2_out15[14], decoder_1_out7[6]);
  and and_18 (and_18_out, decoder_2_out15[14], decoder_1_out7[5]);
  and and_19 (and_19_out, decoder_2_out15[13], decoder_1_out7[6]);
  and and_20 (and_20_out, decoder_2_out15[13], decoder_1_out7[5]);
  and and_21 (and_21_out, decoder_2_out15[12], decoder_1_out7[6]);
  and and_22 (and_22_out, decoder_2_out15[12], decoder_1_out7[5]);
  and and_23 (and_23_out, decoder_2_out15[12], decoder_1_out7[4]);
  and and_24 (and_24_out, decoder_2_out15[11], decoder_1_out7[6]);
  and and_25 (and_25_out, decoder_2_out15[11], decoder_1_out7[5]);
  and and_26 (and_26_out, decoder_2_out15[11], decoder_1_out7[4]);
  and and_27 (and_27_out, decoder_2_out15[11], decoder_1_out7[3]);
  and and_28 (and_28_out, decoder_2_out15[10], decoder_1_out7[6]);
  and and_29 (and_29_out, decoder_2_out15[10], decoder_1_out7[5]);
  and and_30 (and_30_out, decoder_2_out15[9], or_1_out, decoder_1_out7[6]);
  and and_31 (and_31_out, decoder_2_out15[9], or_1_out, decoder_1_out7[5]);
  and and_32 (and_32_out, decoder_2_out15[9], ~or_1_out, decoder_1_out7[6]);  // AND_Gate
  and and_33 (and_33_out, decoder_2_out15[9], ~or_1_out, decoder_1_out7[5]);  // AND_Gate
  and and_34 (FC, decoder_2_out15[8], decoder_1_out7[6]);
  and and_35 (and_35_out, decoder_2_out15[7], decoder_1_out7[6]);
  and and_36 (and_36_out, decoder_2_out15[7], decoder_1_out7[5]);
  and and_37 (and_37_out, decoder_2_out15[6], decoder_1_out7[6]);
  and and_38 (PDO, decoder_2_out15[6], decoder_1_out7[5]);
  and and_39 (and_39_out, decoder_2_out15[5], decoder_1_out7[6]);
  and and_40 (and_40_out, decoder_2_out15[5], decoder_1_out7[5]);
  and and_41 (and_41_out, decoder_2_out15[4], decoder_1_out7[6]);
  and and_42 (PAO, decoder_2_out15[4], decoder_1_out7[5]);
  and and_43 (and_43_out, decoder_2_out15[3], decoder_1_out7[6]);
  and and_44 (SPI, decoder_2_out15[3], decoder_1_out7[5]);
  and and_45 (and_45_out, decoder_2_out15[3], decoder_1_out7[4]);
  and and_46 (and_46_out, decoder_2_out15[2], decoder_1_out7[6]);
  and and_47 (and_47_out, decoder_2_out15[2], decoder_1_out7[5]);
  and and_48 (and_48_out, decoder_2_out15[2], decoder_1_out7[4]);
  and and_49 (and_49_out, decoder_2_out15[1], decoder_1_out7[0]);
  and and_50 (Halt, decoder_2_out15[0], decoder_1_out7[6]);
  and and_51 (and_51_out, decoder_2_out15[15], decoder_1_out7[4]);
  and and_52 (and_52_out, decoder_2_out15[14], decoder_1_out7[4]);
  and and_53 (and_53_out, decoder_2_out15[13], decoder_1_out7[4]);
  and and_54 (and_54_out, decoder_2_out15[12], decoder_1_out7[3]);
  and and_55 (and_55_out, decoder_2_out15[11], decoder_1_out7[2]);
  and and_56 (and_56_out, decoder_2_out15[10], decoder_1_out7[4]);
  and and_57 (and_57_out, decoder_2_out15[9], decoder_1_out7[4]);
  and and_58 (and_58_out, decoder_2_out15[8], decoder_1_out7[5]);
  and and_59 (and_59_out, decoder_2_out15[7], decoder_1_out7[4]);
  and and_60 (and_60_out, decoder_2_out15[6], decoder_1_out7[4]);
  and and_61 (and_61_out, decoder_2_out15[5], decoder_1_out7[4]);
  and and_62 (and_62_out, decoder_2_out15[4], decoder_1_out7[4]);
  and and_63 (and_63_out, decoder_2_out15[3], decoder_1_out7[3]);
  and and_64 (and_64_out, decoder_2_out15[2], decoder_1_out7[3]);
  and and_65 (and_65_out, decoder_2_out15[1], decoder_1_out7[0]);
  and and_66 (and_66_out, decoder_1_out7[2], or_2_out);
  and and_67 (and_67_out, or_2_out, decoder_1_out7[6]);
  and and_68 (and_68_out, or_2_out, decoder_1_out7[5]);
  and and_69 (and_69_out, or_2_out, decoder_1_out7[4]);
  and and_70 (and_70_out, or_2_out, decoder_1_out7[3]);
  and and_71 (and_71_out, decoder_1_out7[3], or_3_out);
  and and_72 (and_72_out, or_3_out, decoder_1_out7[6]);
  and and_73 (and_73_out, or_3_out, decoder_1_out7[5]);
  and and_74 (and_74_out, or_3_out, decoder_1_out7[4]);
  and and_75 (AXC, decoder_3_out15[3], decoder_1_out7[6]);
  and and_76 (and_76_out, decoder_3_out15[3], decoder_1_out7[5]);
  or or_4 (or_4_out, and_69_out, and_73_out);
  or or_5 (FS, and_70_out, and_74_out);
  or or_6 (CounterReset, and_51_out, and_52_out, and_53_out, and_54_out, and_55_out, and_56_out, and_57_out, and_58_out, and_59_out, and_60_out, and_61_out, and_62_out, and_63_out, and_64_out, and_65_out, and_66_out, and_71_out, and_76_out);
  buf buffer_1 (buffer_1_out, and_20_out);
  buf buffer_2 (buffer_2_out, buffer_1_out);
  buf buffer_3 (buffer_3_out, and_23_out);
  buf buffer_4 (buffer_4_out, buffer_3_out);
  buf buffer_5 (buffer_5_out, and_27_out);
  buf buffer_6 (buffer_6_out, buffer_5_out);
  buf buffer_7 (buffer_7_out, and_36_out);
  buf buffer_8 (buffer_8_out, buffer_7_out);
  buf buffer_9 (buffer_9_out, and_40_out);
  buf buffer_10 (buffer_10_out, buffer_9_out);
  buf buffer_11 (buffer_11_out, and_45_out);
  buf buffer_12 (buffer_12_out, buffer_11_out);
  buf buffer_13 (buffer_13_out, and_48_out);
  buf buffer_14 (buffer_14_out, buffer_13_out);
  buf buffer_15 (buffer_15_out, buffer_2_out);
  buf buffer_16 (buffer_16_out, buffer_15_out);
  buf buffer_17 (buffer_17_out, buffer_4_out);
  buf buffer_18 (buffer_18_out, buffer_17_out);
  buf buffer_19 (buffer_19_out, buffer_6_out);
  buf buffer_20 (buffer_20_out, buffer_19_out);
  buf buffer_21 (buffer_21_out, buffer_8_out);
  buf buffer_22 (buffer_22_out, buffer_21_out);
  buf buffer_23 (buffer_23_out, buffer_10_out);
  buf buffer_24 (buffer_24_out, buffer_23_out);
  buf buffer_25 (buffer_25_out, buffer_12_out);
  buf buffer_26 (buffer_26_out, buffer_25_out);
  buf buffer_27 (buffer_27_out, buffer_14_out);
  buf buffer_28 (buffer_28_out, buffer_27_out);
  and and_77 (and_77_out, and_20_out, buffer_29_out);
  buf buffer_29 (buffer_29_out, buffer_16_out);
  and and_78 (and_78_out, and_23_out, buffer_30_out);
  buf buffer_30 (buffer_30_out, buffer_18_out);
  and and_79 (and_79_out, and_27_out, buffer_31_out);
  buf buffer_31 (buffer_31_out, buffer_20_out);
  and and_80 (and_80_out, and_36_out, buffer_32_out);
  buf buffer_32 (buffer_32_out, buffer_22_out);
  and and_81 (and_81_out, and_40_out, buffer_33_out);
  buf buffer_33 (buffer_33_out, buffer_24_out);
  and and_82 (and_82_out, and_45_out, buffer_34_out);
  buf buffer_34 (buffer_34_out, buffer_26_out);
  and and_83 (and_83_out, and_48_out, buffer_35_out);
  buf buffer_35 (buffer_35_out, buffer_28_out);
  buf buffer_36 (buffer_36_out, and_45_out);
  buf buffer_37 (buffer_37_out, and_48_out);
  buf buffer_38 (buffer_38_out, and_45_out);
  buf buffer_39 (buffer_39_out, buffer_38_out);
  buf buffer_40 (buffer_40_out, and_45_out);
  buf buffer_41 (buffer_41_out, buffer_40_out);
  buf buffer_42 (buffer_42_out, and_48_out);
  buf buffer_43 (buffer_43_out, buffer_42_out);
  LED led_1 (.in(IRS));
  LED led_2 (.in(MAE));
  or or_7 (MAE, IRS, and_15_out, and_16_out, and_17_out, and_19_out, and_20_out, and_21_out, and_22_out, and_23_out, and_24_out, and_25_out, and_26_out, and_27_out, and_28_out, and_30_out, and_35_out, FS, and_36_out, and_37_out, PDO, and_39_out, and_40_out, and_41_out, PAO, and_43_out, SPI, buffer_44_out, and_46_out, and_47_out, buffer_45_out, and_67_out, and_68_out, or_4_out);
  LED led_3 (.in(MAE));
  buf buffer_44 (buffer_44_out, buffer_36_out);
  buf buffer_45 (buffer_45_out, buffer_37_out);
  LED led_4 (.in(MDO));
  or or_8 (MDO, IRS, and_15_out, and_16_out, and_17_out, and_19_out, and_21_out, and_22_out, and_24_out, and_25_out, and_26_out, and_28_out, and_30_out, and_35_out, and_37_out, PDO, and_39_out, and_41_out, PAO, and_43_out, SPI, and_46_out, and_47_out, and_67_out, and_68_out, or_4_out, FS);
  LED led_5 (.in(MDO));
  or or_9 (RW, and_77_out, and_78_out, and_79_out, and_80_out, and_81_out, and_82_out, and_83_out);
  LED led_6 (.in(RW));
  or or_10 (PCO, IRS, and_15_out, and_17_out, and_19_out, and_21_out, and_22_out, and_24_out, and_26_out, and_28_out, and_30_out, and_35_out, and_37_out, and_39_out, and_41_out, and_43_out, and_46_out, and_67_out, or_4_out);
  LED led_7 (.in(PCO));
  or or_11 (PCL, and_29_out, and_31_out);
  LED led_8 (.in(PCL));
  or or_12 (PCE, and_15_out, and_16_out, and_17_out, and_18_out, and_19_out, and_20_out, and_21_out, and_22_out, and_23_out, and_24_out, and_26_out, and_27_out, and_28_out, and_30_out, and_32_out, and_33_out, FC, and_35_out, and_36_out, and_37_out, PDO, and_39_out, and_40_out, and_41_out, PAO, and_43_out, SPI, and_46_out, and_47_out, and_49_out, and_67_out, or_4_out, FS);
  LED led_9 (.in(PCE));
  buf buffer_46 (buffer_46_out, buffer_39_out);
  or or_13 (SPO, buffer_46_out, and_47_out);
  LED led_10 (.in(SPO));
  LED led_11 (.in(SPI));
  or or_14 (SPE, SPI, and_48_out);
  LED led_12 (.in(SPE));
  or or_15 (TXS, and_22_out, and_25_out, SPI, and_47_out, and_68_out, and_72_out);
  LED led_13 (.in(TXS));
  or or_16 (TXO, and_23_out, and_27_out, buffer_47_out, buffer_48_out);
  LED led_14 (.in(TXO));
  buf buffer_47 (buffer_47_out, buffer_41_out);
  buf buffer_48 (buffer_48_out, buffer_43_out);
  or or_17 (AXS, and_16_out, and_17_out, FS);
  LED led_15 (.in(AXS));
  or or_18 (AXI, and_16_out, and_17_out);
  LED led_16 (.in(AXI));
  or or_19 (AXO, and_20_out, and_72_out);
  LED led_17 (.in(AXO));
  LED led_18 (.in(AXC));
  or or_20 (IAS, and_15_out, and_19_out, and_21_out, and_24_out, and_26_out, and_28_out, and_30_out, and_35_out, and_37_out, and_39_out, and_41_out, and_43_out, and_46_out, and_67_out, or_4_out);
  LED led_19 (.in(IAS));
  or or_21 (IAE, and_16_out, and_20_out, and_23_out, and_25_out, and_27_out, and_29_out, and_31_out, and_36_out, PDO, and_40_out, PAO, SPI, and_48_out, and_68_out, FS);
  LED led_20 (.in(IAE));
  LED led_21 (.in(FS));
  LED led_22 (.in(FC));
  or or_22 (PDS, and_36_out, PDO);
  LED led_23 (.in(PDS));
  LED led_24 (.in(PDO));
  or or_23 (PAS, and_40_out, PAO);
  LED led_25 (.in(PAS));
  LED led_26 (.in(PAO));
  LED led_27 (.in(Halt));
  LED led_28 (.in(CounterReset));

  assign MDE = MAE;
  assign RR = MDO;

  // Notes on the sheet:
  //   CAEZNPO
endmodule

module TIMU (
  input  Halt,
  input  Reset,
  input  Clock,
  output [2:0] StepOutput
);

  wire and_1_out, d_ff_1_q, not_1_out;
  wire [2:0] pull_resistor_1_node;

  not not_1 (not_1_out, Halt);
  D_Flip_Flop d_ff_1 (.D(not_1_out), .clk(Clock), .Q(d_ff_1_q), .reset(Reset));  // open: Qn, preset
  and and_1 (and_1_out, Clock, d_ff_1_q);
  Pull_Resistor pull_resistor_1 (.node(pull_resistor_1_node));
  Counter #(.max('h7), .trigger("falling"), .width(3)) counter_1 (
    .clr(Reset), .load(1'b0), .up(1'b1), .count(1'b1), .clk(and_1_out), .D(pull_resistor_1_node),
    .Q(StepOutput));  // open: carry
endmodule

module flagmatching (
  input  [3:0] FlagOpcodes,
  input  [6:0] ALUFlags
);

  wire and_1_out, and_2_out, and_3_out, and_4_out, and_5_out, and_6_out, and_7_out, and_8_out, and_9_out,
       and_10_out, and_11_out, and_12_out, and_13_out, and_14_out;

  and and_1 (and_1_out, ~FlagOpcodes[3], ~FlagOpcodes[2], ALUFlags[6], ~FlagOpcodes[1], ~FlagOpcodes[0]);  // AND_Gate
  and and_2 (and_2_out, ~FlagOpcodes[3], ~FlagOpcodes[2], ~ALUFlags[6], ~FlagOpcodes[1], FlagOpcodes[0]);  // AND_Gate
  and and_3 (and_3_out, ~FlagOpcodes[3], ~FlagOpcodes[2], ALUFlags[5], FlagOpcodes[1], ~FlagOpcodes[0]);  // AND_Gate
  and and_4 (and_4_out, ~FlagOpcodes[3], ~FlagOpcodes[2], ~ALUFlags[5], FlagOpcodes[1], FlagOpcodes[0]);  // AND_Gate
  and and_5 (and_5_out, ~FlagOpcodes[3], FlagOpcodes[2], ALUFlags[4], ~FlagOpcodes[1], ~FlagOpcodes[0]);  // AND_Gate
  and and_6 (and_6_out, ~FlagOpcodes[3], FlagOpcodes[2], ~ALUFlags[4], ~FlagOpcodes[1], FlagOpcodes[0]);  // AND_Gate
  and and_7 (and_7_out, ~FlagOpcodes[3], FlagOpcodes[2], ALUFlags[3], FlagOpcodes[1], ~FlagOpcodes[0]);  // AND_Gate
  and and_8 (and_8_out, ~FlagOpcodes[3], FlagOpcodes[2], ~ALUFlags[3], FlagOpcodes[1], FlagOpcodes[0]);  // AND_Gate
  and and_9 (and_9_out, FlagOpcodes[3], ~FlagOpcodes[2], ALUFlags[2], ~FlagOpcodes[1], ~FlagOpcodes[0]);  // AND_Gate
  and and_10 (and_10_out, FlagOpcodes[3], ~FlagOpcodes[2], ~ALUFlags[2], ~FlagOpcodes[1], FlagOpcodes[0]);  // AND_Gate
  and and_11 (and_11_out, FlagOpcodes[3], ~FlagOpcodes[2], ALUFlags[1], FlagOpcodes[1], ~FlagOpcodes[0]);  // AND_Gate
  and and_12 (and_12_out, FlagOpcodes[3], ~FlagOpcodes[2], ~ALUFlags[1], FlagOpcodes[1], FlagOpcodes[0]);  // AND_Gate
  and and_13 (and_13_out, FlagOpcodes[3], FlagOpcodes[2], ALUFlags[0], ~FlagOpcodes[1], ~FlagOpcodes[0]);  // AND_Gate
  and and_14 (and_14_out, FlagOpcodes[3], FlagOpcodes[2], ~ALUFlags[0], ~FlagOpcodes[1], FlagOpcodes[0]);  // AND_Gate
  // OR_Gate or_1 has open pins: in0=and_1_out, in1=and_2_out, in2=and_3_out, in3=and_4_out, in4=and_5_out, in5=and_6_out, in6=and_7_out, in7=and_8_out, in8=and_9_out, in9=and_10_out, in10=and_11_out, in11=and_12_out, in12=and_13_out, in13=and_14_out, out=open

  // Notes on the sheet:
  //   CAEZNPO
endmodule

module testcirc (
  input  [6:0] in_1,
  input  [3:0] in_2
);

  wire clock_1_out, testaxc, testaxi, testaxo, testaxs, testfc, testfs, testiae, testias, testirs, testmae,
       testmde, testmdo, testpao, testpas, testpce, testpcl, testpco, testpdo, testpds, testrr, testrw,
       testspe, testspi, testspo, testtxo, testtxs;
  wire [3:3] pull_resistor_1_node;
  wire [7:0] counter_1_q;

  Counter #(.trigger("falling")) counter_1 (
    .clr(1'b0), .load(1'b0), .up(1'b1), .count(1'b1), .clk(clock_1_out), .Q(counter_1_q));  // open: D, carry
  Clock clock_1 (.out(clock_1_out));
  LED led_1 (.in(counter_1_q[7]));
  Hex_Digit_Display #(.decimalPoint("false")) hex_digit_display_1 (.value({pull_resistor_1_node[3], counter_1_q[2:0]}));
  Pull_Resistor pull_resistor_1 (.node(pull_resistor_1_node[3]));
  CU cu_1 (
    .Instruction({counter_1_q[7:3], in_2}), .Flags(in_1), .ClockCycle(counter_1_q[2:0]), .IRS(testirs),
    .PCL(testpcl), .PCE(testpce), .SPO(testspo), .SPI(testspi), .SPE(testspe), .TXS(testtxs), .TXO(testtxo),
    .AXS(testaxs), .AXI(testaxi), .AXO(testaxo), .AXC(testaxc), .IAS(testias), .IAE(testiae), .FS(testfs),
    .FC(testfc), .PDS(testpds), .PDO(testpdo), .PAS(testpas), .PAO(testpao), .MAE(testmae), .MDE(testmde),
    .MDO(testmdo), .RR(testrr), .RW(testrw), .PCO(testpco));  // open: Halt, CounterReset
  LED led_2 (.in(counter_1_q[6]));
  LED led_3 (.in(counter_1_q[5]));
  LED led_4 (.in(counter_1_q[4]));
  LED led_5 (.in(counter_1_q[3]));
  LED led_6 (.in(testirs));
  LED led_7 (.in(testmae));
  LED led_8 (.in(testmde));
  LED led_9 (.in(testmdo));
  LED led_10 (.in(testrr));
  LED led_11 (.in(testrw));
  LED led_12 (.in(testpco));
  LED led_13 (.in(testpcl));
  LED led_14 (.in(testpce));
  LED led_15 (.in(testspo));
  LED led_16 (.in(testspi));
  LED led_17 (.in(testspe));
  LED led_18 (.in(testtxs));
  LED led_19 (.in(testtxo));
  LED led_20 (.in(testaxs));
  LED led_21 (.in(testaxc));
  LED led_22 (.in(testias));
  LED led_23 (.in(testaxi));
  LED led_24 (.in(testaxo));
  LED led_25 (.in(testiae));
  LED led_26 (.in(testfs));
  LED led_27 (.in(testfc));
  LED led_28 (.in(testpds));
  LED led_29 (.in(testpdo));
  LED led_30 (.in(testpas));
  LED led_31 (.in(testpao));

  // Other names for the same wires on the sheet: testflaginput[6:0] = in_1

  // Notes on the sheet:
  //   NB: MASIH BELUM DI-TES ULANG SETELAH REVISI PADA 22/4/2025
  //   Cycle
  //   Instruction
endmodule
